# Fritzing sketch DCmotor (saved by Fritzing 0.7.0b)
breadboards: 1

parts:
  Arduino1 = Arduino
  M1 = DC Motor
  IC1 = H-Bridge [package=THT]
  C1 = Ceramic Capacitor [capacitance=0.1µF voltage=10V package="100 mil [THT, multilayer]"]

nets:
  N1: Arduino1.D11, IC1.1_2EN
  N2: Arduino1.D10, IC1.1A
  N3: Arduino1.D9, IC1.2A
  N4: Arduino1.+5V, IC1.VCC2, IC1.VCC1, C1.0
  GND: Arduino1.GND, IC1.GND1, IC1.GND2, IC1.GND3, IC1.GND4, C1.1
  N5: M1.pin_1, IC1.2Y
  N6: M1.pin_2, IC1.1Y

notes:
  10k pulldown resistor
