# Fritzing sketch HMC6352 (saved by Fritzing 0.7.0b)
breadboards: 4

parts:
  Arduino2 = Arduino Fio  # not connected
  Arduino3 = Arduino Fio  # not connected
  Part4 = Arduino Pro Mini 3.3V
  Part5 = FTDI Basic Programmer
  Part10 = Compass Module - HMC6352  # not connected
  Part11 = Compass Module - HMC6352  # not connected
  Part12 = Compass Module - HMC6352  # not connected
  Arduino4 = Arduino
  Part13 = Compass Module - HMC6352

nets:
  N1: Part4.DTR, Part5.DTR
  N2: Part4.TXO, Part5.RXI
  N3: Part4.RXI, Part5.TXO
  N4: Part4.VCC, Part5.POWER
  GND: Part4.GND, Part5.CTS, Part5.GND
  +5V: Arduino4.+5V, Part13.VCC
  GND_2: Arduino4.GND, Part13.GND
  N5: Arduino4.A4, Part13.SDA
  N6: Arduino4.A5, Part13.SCL
