# Fritzing sketch ITG3200 (saved by Fritzing 0.7.0b)
breadboards: 4

parts:
  Arduino2 = Arduino Fio
  Part2 = Triple Axis Gyro Breakout ITG-3200
  S1 = Pushbutton [package="[THT]"]
  R1 = Resistor [tolerance=±5% resistance=10k package=THT]
  Arduino3 = Arduino Fio
  S2 = Pushbutton [package="[THT]"]
  R2 = Resistor [tolerance=±5% resistance=10k package=THT]
  Part3 = Triple Axis Gyro Breakout ITG-3200  # not connected
  Part4 = Arduino Pro Mini 3.3V
  Part5 = FTDI Basic Programmer
  Part6 = Triple Axis Gyro Breakout ITG-3200
  S3 = Pushbutton [package="[THT]"]
  R3 = Resistor [tolerance=±5% resistance=10k package=THT]
  Part7 = Triple Axis Gyro Breakout ITG-3200
  Arduino4 = Arduino
  S4 = Pushbutton [package="[THT]"]
  R4 = Resistor [tolerance=±5% resistance=10k package=THT]

nets:
  N1: Arduino2.A5, Part2.SCL
  N2: Arduino2.A4, Part2.SDA
  3V3: Arduino2.3V3, Arduino2.D11, Part2.VCC, Part2.VLOGIC, S1.Pin_1, S1.Pin_2, R1.Pin_1
  GND: Arduino2.GND, Part2.GND, R1.Pin_0
  N3: S1.Pin_3, S1.Pin_4
  N4: Arduino3.A5, Arduino3.D2, S2.Pin_1, S2.Pin_2, R2.Pin_0
  N5: Arduino3.AREF, R2.Pin_1
  N6: S2.Pin_3, S2.Pin_4
  N7: Part4.DTR, Part5.DTR
  N8: Part4.TXO, Part5.RXI
  N9: Part4.RXI, Part5.TXO
  VCC: Part4.VCC, Part5.POWER, Part6.VCC, Part6.VLOGIC, S3.Pin_3, S3.Pin_4
  GND_2: Part4.GND, Part5.CTS, Part5.GND, Part6.GND, R3.Pin_1
  N10: Part4.A4, Part6.SDA
  N11: Part4.A5, Part6.SCL
  N12: Part4.MOSI, S3.Pin_1, S3.Pin_2, R3.Pin_0
  VCC_2: Part7.VCC, Part7.VLOGIC, Arduino4.3V3
  GND_3: Part7.GND, Arduino4.GND, R4.Pin_1
  N13: Arduino4.D11, S4.Pin_3, S4.Pin_4, R4.Pin_0
  N14: Arduino4.+5V, S4.Pin_1, S4.Pin_2
