# Fritzing sketch Stepper_easydriver (saved by Fritzing 0.7.7b)

parts:
  Arduino1 = Arduino
  Part1 = EasyDriver_v44
  Power_plug1 = Power plug
  M1 = Stepper Motor - Bipolar

nets:
  N1: Arduino1.D3, Part1.STEP
  N2: Arduino1.D2, Part1.DIR
  GND: Arduino1.GND, Part1.GND, Power_plug1.GND
  N3: Part1.V+, Power_plug1.VCC
  N4: Part1.OUT2A, M1.A
  N5: Part1.OUT2B, M1.C
  N6: Part1.OUT1A, M1.B
  N7: Part1.OUT1B, M1.D

notes:
  10k pulldown resistor
  Motor Power Supply
