# Fritzing sketch analog_accelerometer (saved by Fritzing 0.7.0b)
breadboards: 1

parts:
  Arduino1 = Arduino
  Part1 = Triple Axis Accelerometer Breakout - ADXL335
  S1 = Pushbutton [package="[THT]"]
  R1 = Resistor [tolerance=±5% resistance=10k package=THT]

nets:
  3V3: Arduino1.aref, Arduino1.3V3, Part1.VCC, S1.Pin_1, S1.Pin_2
  N1: Arduino1.D2, S1.Pin_3, S1.Pin_4, R1.Pin_1
  GND: Arduino1.GND, Part1.ST, Part1.GND, R1.Pin_0
  N2: Arduino1.A0, Part1.XOUT
  N3: Arduino1.A1, Part1.YOUT
  N4: Arduino1.A2, Part1.ZOUT
