# Fritzing sketch bi_color_led (saved by Fritzing 0.7.4b)
breadboards: 1

parts:
  Arduino1 = Arduino
  LED1 = DUO LED RG (com. cathode, rbg) [package="5 mm [THT]"]
  R1 = Resistor [tolerance=±5% resistance=330 package=THT]
  R3 = Resistor [tolerance=±5% resistance=330 package=THT]

nets:
  N1: Arduino1.GND, LED1.common_cathode
  N2: Arduino1.D11, R3.Pin_0
  N3: Arduino1.D10, R1.Pin_0
  N4: LED1.red_anode, R3.Pin_1
  N5: LED1.green_anode, R1.Pin_1

notes:
  10k potentiometer

custom parts:
  DUO LED RG (com. cathode, rbg): A 5mm DUO-color LED with red and green inside. Pin order: red - com. cathode - green
