# Fritzing sketch flex (saved by Fritzing 0.7.0b)
breadboards: 1

parts:
  Arduino1 = Arduino
  R2 = Resistor [resistance=10k tolerance=±5% package=THT]
  R3 = Basic Flex Resistor

nets:
  N1: Arduino1.+5V, R3.Pin_2
  N2: Arduino1.GND, R2.Pin_1
  N3: Arduino1.A0, R2.Pin_0, R3.pin_1

notes:
  10k potentiometer
