# Fritzing sketch fsr (saved by Fritzing 0.7.0b)
breadboards: 1

parts:
  Arduino1 = Arduino
  R2 = Resistor [resistance=10k tolerance=±5% package=THT]
  J1 = Basic Force Sensing Resistor (FSR) [package=THT]

nets:
  N1: Arduino1.+5V, J1.pin_1
  N2: Arduino1.GND, R2.Pin_1
  N3: Arduino1.A0, R2.Pin_0, J1.pin_0

notes:
  10k potentiometer
