# Fritzing sketch generator (saved by Fritzing 0.7.0b)
breadboards: 1

parts:
  R1 = Resistor [resistance=330 tolerance=±5% package=THT]
  LED1 = Red LED - 5mm [package="5 mm [THT]"]
  R2 = Resistor [resistance=330 tolerance=±5% package=THT]
  Arduino1 = Arduino
  LED2 = Red LED - 5mm [package="5 mm [THT]"]

nets:
  N1: R1.Pin_0, LED2.cathode
  N2: R1.Pin_1, R2.Pin_1, Arduino1.GND
  N3: LED1.cathode, R2.Pin_0
  N4: LED1.anode, Arduino1.D11
  N5: Arduino1.D7, LED2.anode

notes:
  10k pulldown resistor
