# Fritzing sketch getting_started (saved by Fritzing 0.7.4b)
breadboards: 1

parts:
  Arduino1 = Arduino
  R1 = Rotary Potentiometer (Large) [package=THT]
  LED1 = LED - 5mm [color="Red (633nm)" package="5 mm [THT]"]
  R2 = Resistor [tolerance=±5% resistance=330 package=THT]
  S1 = Pushbutton [package="[THT]"]
  R3 = Resistor [tolerance=±5% resistance=10k package=THT]

nets:
  N1: Arduino1.D11, LED1.anode
  N2: Arduino1.D2, S1.Pin_3, S1.Pin_4, R3.Pin_0
  N3: Arduino1.+5V, R1.leg2, S1.Pin_1, S1.Pin_2
  N4: Arduino1.GND, R1.leg1, R2.Pin_1, R3.Pin_1
  N5: Arduino1.A0, R1.wiper
  N6: LED1.cathode, R2.Pin_0

notes:
  10k potentiometer
