# Fritzing sketch hello_world (saved by Fritzing 0.7.0b)
breadboards: 1

parts:
  S1 = Pushbutton [package="[THT]"]
  R1 = Resistor [resistance=10k tolerance=±5% package=THT]
  LED1 = Red LED - 5mm [package="5 mm [THT]"]
  R2 = Resistor [resistance=330 tolerance=±5% package=THT]
  Arduino1 = Arduino

nets:
  N1: S1.Pin_1, S1.Pin_2, R1.Pin_0, Arduino1.D2
  N2: S1.Pin_3, S1.Pin_4, Arduino1.+5V
  N3: R1.Pin_1, R2.Pin_1, Arduino1.GND
  N4: LED1.cathode, R2.Pin_0
  N5: LED1.anode, Arduino1.D11

notes:
  10k pulldown resistor
