# Fritzing sketch led (saved by Fritzing 0.7.7b)
breadboards: 1

parts:
  Arduino1 = Arduino
  LED1 = LED - 5mm [color="Red (633nm)" package="5 mm [THT]"]
  R1 = Resistor [tolerance=±5% resistance=220 package=THT]
  Arduino2 = Arduino
  R2 = Resistor [tolerance=±5% resistance=220 package=THT]
  LED2 = LED - 5mm [color="Red (633nm)" package="5 mm [THT]"]

nets:
  N1: Arduino1.D11, R1.Pin_1
  N2: Arduino1.GND, LED1.cathode
  N3: LED1.anode, R1.Pin_0
  N4: Arduino2.GND, LED2.cathode
  N5: Arduino2.D11, R2.Pin_0

notes:
  10k potentiometer
