# Fritzing sketch leonardo (saved by Fritzing 0.7.4b)
breadboards: 1

parts:
  Part1 = Compass Module - HMC6352
  LED1 = LED - 5mm [color="Red (633nm)" package="5 mm [THT]"]
  LED2 = LED - 5mm [color="Red (633nm)" package="5 mm [THT]"]
  R1 = Rotary Potentiometer (Large) [maximum_resistance=100kΩ package=THT]
  R2 = Resistor [tolerance=±5% resistance=330 package=THT]
  R3 = Resistor [tolerance=±5% resistance=330 package=THT]
  S1 = Pushbutton [package="[THT]"]
  R4 = Resistor [tolerance=±5% resistance=10k package=THT]
  S2 = Pushbutton [package="[THT]"]
  R5 = Resistor [tolerance=±5% resistance=10k package=THT]
  J1 = Basic Servo
  Arduino1 = Arduino

nets:
  GND: Part1.GND, R1.leg2, R2.Pin_0, R3.Pin_0, S1.Pin_3, S1.Pin_4, R4.Pin_0, R4.Pin_1, R5.Pin_1, J1.gnd, Arduino1.GND, Arduino1.A2
  VCC: Part1.VCC, R1.leg1, S1.Pin_1, S1.Pin_2, S2.Pin_1, S2.Pin_2, J1.vcc, Arduino1.+5V
  N1: Part1.SDA, Arduino1.SDA
  N2: Part1.SCL, Arduino1.SCL
  N3: LED1.cathode, R2.Pin_1
  N4: LED1.anode, Arduino1.D13
  N5: LED2.cathode, R3.Pin_1
  N6: LED2.anode, Arduino1.D1TX
  N7: R1.wiper, Arduino1.D4
  N8: S2.Pin_3, S2.Pin_4, R5.Pin_0, Arduino1.D0RX
  N9: J1.pulse, Arduino1.D9
