# Fritzing sketch mega (saved by Fritzing 0.7.0b)
breadboards: 1

parts:
  Part1 = Compass Module - HMC6352
  J1 = Basic Servo
  LED1 = LED - 5mm [color="Red (633nm)" package="5 mm [THT]"]
  R1 = Rotary Potentiometer (Large) [maximum_resistance=100kΩ package=THT]
  R2 = Resistor [tolerance=±5% resistance=330 package=THT]
  S1 = Pushbutton [package="[THT]"]
  R4 = Resistor [tolerance=±5% resistance=10k package=THT]
  S2 = Pushbutton [package="[THT]"]
  R5 = Resistor [tolerance=±5% resistance=10k package=THT]
  Arduino1 = Arduino Mega
  Part2 = Compass Module - HMC6352

nets:
  GND: Part1.GND, J1.gnd, R1.leg2, R2.Pin_0, R5.Pin_1, Arduino1.GND, Part2.GND
  VCC: Part1.VCC, J1.vcc, R1.leg1, S1.Pin_1, S1.Pin_2, S2.Pin_1, S2.Pin_2, Arduino1.+5V, Part2.VCC
  N1: Part1.SDA, Arduino1.D20, Part2.SDA
  N2: Part1.SCL, Arduino1.D21, Part2.SCL
  N3: J1.pulse, Arduino1.D4
  N4: LED1.cathode, R2.Pin_1
  N5: LED1.anode, Arduino1.D11
  N6: R1.wiper, Arduino1.A15
  N7: S1.Pin_3, S1.Pin_4, R4.Pin_0, Arduino1.A2
  N8: S2.Pin_3, S2.Pin_4, R5.Pin_0, Arduino1.D37
