# Fritzing sketch rgbled_common_anode (saved by Fritzing 0.7.0b)
breadboards: 1

parts:
  R1 = Resistor [resistance=330 tolerance=±5% package=THT]
  R1_2 = Resistor [resistance=330 tolerance=±5% package=THT]
  Arduino1 = Arduino
  LED1 = RGB LED Common Cathode - (4 legs) [package="5 mm [THT]"]
  R1_3 = Resistor [resistance=330 tolerance=±5% package=THT]
  S1 = Pushbutton [package="[THT]"]
  R2 = Resistor [tolerance=±5% resistance=10k package=THT]

nets:
  N1: R1.Pin_0, Arduino1.D10
  N2: R1.Pin_1, LED1.green_anode
  N3: R1_2.Pin_0, Arduino1.D9
  N4: R1_2.Pin_1, LED1.red_anode
  N5: Arduino1.GND, R2.Pin_1
  N6: Arduino1.D11, R1_3.Pin_0
  N7: Arduino1.D2, S1.Pin_3, S1.Pin_4, R2.Pin_0
  N8: Arduino1.+5V, LED1.common_cathode, S1.Pin_1, S1.Pin_2
  N9: LED1.blue_anode, R1_3.Pin_1

notes:
  10k potentiometer

custom parts:
  RGB LED Common Cathode - (4 legs): A 5mm tri-color LED with red, green and blue inside.
