# Fritzing sketch sharp_IR (saved by Fritzing 0.7.0b)
breadboards: 1

parts:
  Arduino1 = Arduino
  C1 = Electrolytic Capacitor [package=THT]
  J1 = Infrared Proximity Sensor

nets:
  +5V: Arduino1.+5V, C1.+, J1.Vcc
  GND: Arduino1.GND, C1.-, J1.GND
  N1: Arduino1.A0, J1.Vout

notes:
  10k potentiometer
