# Fritzing sketch sonar (saved by Fritzing 0.7.1b)
breadboards: 1

parts:
  Arduino1 = Arduino
  J1 = female pin header, 7 pins [form="♀ (female)"]

nets:
  N1: Arduino1.+5V, J1.pin6
  N2: Arduino1.GND, J1.pin7
  N3: Arduino1.A0, J1.pin3

notes:
  10k potentiometer
