# Fritzing sketch teensy (saved by Fritzing 0.7.0b)
breadboards: 1

parts:
  Teensy1 = Teensy 2.0
  Part1 = Compass Module - HMC6352
  J1 = Basic Servo
  LED1 = LED - 5mm [color="Red (633nm)" package="5 mm [THT]"]
  LED2 = LED - 5mm [color="Red (633nm)" package="5 mm [THT]"]
  R1 = Rotary Potentiometer (Large) [maximum_resistance=100kΩ package=THT]
  R2 = Resistor [tolerance=±5% resistance=330 package=THT]
  R3 = Resistor [tolerance=±5% resistance=330 package=THT]
  S1 = Pushbutton [package="[THT]"]
  R4 = Resistor [tolerance=±5% resistance=10k package=THT]
  S2 = Pushbutton [package="[THT]"]
  R5 = Resistor [tolerance=±5% resistance=10k package=THT]

nets:
  GND: Teensy1.GND, Part1.GND, J1.gnd, R1.leg1, R2.Pin_0, R3.Pin_0, R4.Pin_1, R5.Pin_0
  N1: Teensy1.B2, S2.Pin_3, S2.Pin_4, R5.Pin_1
  N2: Teensy1.B7, LED1.anode
  N3: Teensy1.D0, Part1.SCL
  N4: Teensy1.D1, Part1.SDA
  N5: Teensy1.C6, J1.pulse
  N6: Teensy1.C7, LED2.anode
  VCC: Teensy1.VCC, Part1.VCC, J1.vcc, R1.leg2, S1.Pin_1, S1.Pin_2, S2.Pin_1, S2.Pin_2
  N7: Teensy1.F7, S1.Pin_3, S1.Pin_4, R4.Pin_0
  N8: Teensy1.F4, R1.wiper
  N9: LED1.cathode, R2.Pin_1
  N10: LED2.cathode, R3.Pin_1
