# Fritzing sketch temperature (saved by Fritzing 0.7.0b)
breadboards: 1

parts:
  Arduino1 = Arduino
  R2 = Resistor [resistance=330 tolerance=±5% package=THT]
  T1 = LM35 Temperature Sensor [package="TO92 [THT]"]

nets:
  N1: Arduino1.+5V, R2.Pin_1
  GND: Arduino1.GND, T1.GND
  N2: Arduino1.A0, R2.Pin_0, T1.Vout

notes:
  10k potentiometer
