# Fritzing sketch uno (saved by Fritzing 0.7.0b)
breadboards: 1

parts:
  Part1 = Compass Module - HMC6352
  LED1 = LED - 5mm [color="Red (633nm)" package="5 mm [THT]"]
  LED2 = LED - 5mm [color="Red (633nm)" package="5 mm [THT]"]
  R1 = Rotary Potentiometer (Large) [maximum_resistance=100kΩ package=THT]
  R2 = Resistor [tolerance=±5% resistance=330 package=THT]
  R3 = Resistor [tolerance=±5% resistance=330 package=THT]
  S1 = Pushbutton [package="[THT]"]
  R4 = Resistor [tolerance=±5% resistance=10k package=THT]
  S2 = Pushbutton [package="[THT]"]
  R5 = Resistor [tolerance=±5% resistance=10k package=THT]
  Arduino1 = Arduino
  LED3 = RGB LED (com. cathode, rbg) [package="5 mm [THT]"]
  R6 = Resistor [tolerance=±5% resistance=330 package=THT]
  R7 = Resistor [tolerance=±5% resistance=330 package=THT]
  R8 = Resistor [tolerance=±5% resistance=330 package=THT]
  J1 = Basic Servo

nets:
  GND: Part1.GND, R1.leg2, R2.Pin_0, R3.Pin_0, S1.Pin_3, S1.Pin_4, R4.Pin_0, R4.Pin_1, R5.Pin_1, Arduino1.GND, Arduino1.A2, LED3.common_cathode, J1.gnd
  VCC: Part1.VCC, R1.leg1, S1.Pin_1, S1.Pin_2, S2.Pin_1, S2.Pin_2, Arduino1.+5V, J1.vcc
  N1: Part1.SDA, Arduino1.A4
  N2: Part1.SCL, Arduino1.A5
  N3: LED1.cathode, R2.Pin_1
  N4: LED1.anode, Arduino1.D11
  N5: LED2.cathode, R3.Pin_1
  N6: LED2.anode, Arduino1.D10
  N7: R1.wiper, Arduino1.A0
  N8: S2.Pin_3, S2.Pin_4, R5.Pin_0, Arduino1.D2
  N9: Arduino1.D9, J1.pulse
  N10: Arduino1.D6, R6.Pin_1
  N11: Arduino1.D5, R8.Pin_1
  N12: Arduino1.D3, R7.Pin_1
  N13: LED3.red_anode, R7.Pin_0
  N14: LED3.blue_anode, R8.Pin_0
  N15: LED3.green_anode, R6.Pin_0
